# Fritzing sketch schematic (saved by Fritzing 0.9.9b)
breadboards: 1

parts:
  Bluetooth_HC-05 = Bluetooth HC-05 Macho
  Hüvelykujj = mystery part, 3 pins [chip_label=49E]
  Mutatóujj = mystery part, 3 pins [chip_label=49E]
  Középső_ujj = mystery part, 3 pins [chip_label=49E]
  Gyűrűs_ujj = mystery part, 3 pins [chip_label=49E]
  Kisujj = mystery part, 3 pins [chip_label=49E]
  Part2 = USB LiPoly Charger
  Li-Po_akkumulátor = Battery Holders [package=battery-aaa]
  U1 = mystery part, 3 pins [chip_label=Step-up]
  Kapcsoló = SWITCH-SPST-2 [package=switch-spst-vertical]
  Part1 = Arduino Micro (Rev3)
  Mutatóujj-középsőujj_érintőfelület = SWITCH-SPST-2 [package=switch-spst-vertical]
  Hüvelykujj-mutatóujj_érintőfelület = SWITCH-SPST-2 [package=switch-spst-vertical]

nets:
  N1: Bluetooth_HC-05.TXD, Part1.D5_PWM
  VCC: Bluetooth_HC-05.VCC, Part1.3V3
  GND: Bluetooth_HC-05.GND, Hüvelykujj.pin2, Mutatóujj.pin2, Középső_ujj.pin2, Gyűrűs_ujj.pin2, Kisujj.pin2, Part2.GND, Li-Po_akkumulátor.-, Kapcsoló.P, Part1.GND, Mutatóujj-középsőujj_érintőfelület.O, Hüvelykujj-mutatóujj_érintőfelület.O
  N2: Hüvelykujj.pin1, Mutatóujj.pin1, Középső_ujj.pin1, Gyűrűs_ujj.pin1, Kisujj.pin1, Part1.5V
  N3: Hüvelykujj.pin3, Part1.A0
  N4: Mutatóujj.pin3, Part1.A1
  N5: Középső_ujj.pin3, Part1.A2
  N6: Gyűrűs_ujj.pin3, Part1.A3
  N7: Part2.VBAT, Li-Po_akkumulátor.+, U1.pin2
  N8: U1.pin1, Kapcsoló.O
  N9: Part1.RXLED/SS, Mutatóujj-középsőujj_érintőfelület.P
  N10: Part1.D10_PWM/A10, Hüvelykujj-mutatóujj_érintőfelület.P
